// Logisim project ex5.circ as structural Verilog: 1 circuit, main circuit Running_LED
module Running_LED (
  input  [7:0] INITIAL_LED,
  input  RST,
  output [7:0] OUT_LED
);

  wire clock_1_out;

  Clock clock_1 (.out(clock_1_out));
  LED led_1 (.in(OUT_LED[7]));
  LED led_2 (.in(OUT_LED[6]));
  LED led_3 (.in(OUT_LED[5]));
  LED led_4 (.in(OUT_LED[4]));
  LED led_5 (.in(OUT_LED[3]));
  LED led_6 (.in(OUT_LED[2]));
  LED led_7 (.in(OUT_LED[1]));
  LED led_8 (.in(OUT_LED[0]));

  // Notes on the sheet:
  //   PUT CIRCUITS HERE
endmodule
