// Logisim project Q3.circ as structural Verilog: 1 circuit, main circuit main
module main (
  input  CS2,
  input  CS1,
  input  CS0,
  input  in_put,
  output NS2,
  output NS1,
  output NS0,
  output out_put
);

  wire and_1_out, and_2_out, and_3_out, and_4_out, and_5_out, and_7_out, and_8_out, not_1_out, not_2_out,
       not_3_out, not_4_out, not_5_out, not_6_out, or_1_out, or_3_out;

  not not_1 (not_1_out, CS2);
  not not_2 (not_2_out, CS1);
  not not_3 (not_3_out, CS0);
  not not_4 (not_4_out, in_put);
  and and_1 (and_1_out, not_3_out, not_4_out);
  and and_2 (and_2_out, CS2, CS0);
  and and_3 (and_3_out, not_2_out, and_1_out);
  and and_4 (and_4_out, not_2_out, not_3_out);
  and and_5 (and_5_out, not_1_out, and_3_out);
  or or_1 (or_1_out, CS2, and_4_out);
  not not_5 (not_5_out, NS1);
  not not_6 (not_6_out, NS0);
  or or_2 (NS1, and_2_out, and_5_out);
  and and_6 (NS0, or_1_out, in_put);
  and and_7 (and_7_out, not_5_out, not_6_out);
  or or_3 (or_3_out, and_7_out, and_8_out);
  and and_8 (and_8_out, NS1, NS0);
  and and_9 (out_put, 1'b1, or_3_out);

  assign NS2 = 1'b1;
endmodule
